// Digital circuit test0.dig as structural Verilog
module test0 (
  input  ROM,
  input  DEV,
  output CS_RAM,
  output CS_DEV,
  output CS_ROM
);

  wire nand_2_out;

  nand nand_1 (CS_RAM, ROM, ROM);
  nand nand_2 (nand_2_out, DEV, DEV);
  nand nand_3 (CS_ROM, DEV, CS_RAM);
  nand nand_4 (CS_DEV, nand_2_out, CS_RAM);
endmodule
